// Digital circuit 1Bit.dig as structural Verilog
module _1Bit (
  input  CLK,
  input  D,
  input  EN,
  output OUT
);

  wire and_1_out, and_2_out, nand_1_out, nand_2_out, nand_3_out, nand_4_out, nand_5_out, nand_6_out,
       nand_8_out, not_1_out, not_2_out, not_3_out;

  not not_1 (not_1_out, D);
  and and_1 (and_1_out, D, EN);
  and and_2 (and_2_out, EN, not_1_out);
  not not_2 (not_2_out, CLK);
  nand nand_1 (nand_1_out, not_2_out, and_1_out);
  nand nand_2 (nand_2_out, and_2_out, not_2_out);
  nand nand_3 (nand_3_out, nand_1_out, nand_4_out);
  nand nand_4 (nand_4_out, nand_3_out, nand_2_out);
  not not_3 (not_3_out, not_2_out);
  nand nand_5 (nand_5_out, nand_3_out, not_3_out);
  nand nand_6 (nand_6_out, nand_4_out, not_3_out);
  nand nand_7 (OUT, nand_5_out, nand_8_out);
  nand nand_8 (nand_8_out, OUT, nand_6_out);
endmodule
