// Digital circuit Addition.dig as structural Verilog
module Addition (
  input  CIN,
  input  [15:0] A,
  input  [15:0] B,
  output [15:0] SUM,
  output COUT
);

  wire full_adder_1_carry, full_adder_2_carry, full_adder_3_carry, full_adder_4_carry, full_adder_5_carry,
       full_adder_6_carry, full_adder_7_carry, full_adder_8_carry, full_adder_9_carry, full_adder_10_carry,
       full_adder_11_carry, full_adder_12_carry, full_adder_13_carry, full_adder_14_carry,
       full_adder_15_carry;

  FULL_ADDER full_adder_1 (.SUM(SUM[0]), .CARRY(full_adder_1_carry), .C(CIN), .A(A[0]), .B(B[0]));
  FULL_ADDER full_adder_2 (.SUM(SUM[1]), .CARRY(full_adder_2_carry), .C(full_adder_1_carry), .A(A[1]), .B(B[1]));
  FULL_ADDER full_adder_3 (.SUM(SUM[2]), .CARRY(full_adder_3_carry), .C(full_adder_2_carry), .A(A[2]), .B(B[2]));
  FULL_ADDER full_adder_4 (.SUM(SUM[3]), .CARRY(full_adder_4_carry), .C(full_adder_3_carry), .A(A[3]), .B(B[3]));
  FULL_ADDER full_adder_5 (.SUM(SUM[4]), .CARRY(full_adder_5_carry), .C(full_adder_4_carry), .A(A[4]), .B(B[4]));
  FULL_ADDER full_adder_6 (.SUM(SUM[5]), .CARRY(full_adder_6_carry), .C(full_adder_5_carry), .A(A[5]), .B(B[5]));
  FULL_ADDER full_adder_7 (.SUM(SUM[6]), .CARRY(full_adder_7_carry), .C(full_adder_6_carry), .A(A[6]), .B(B[6]));
  FULL_ADDER full_adder_8 (.SUM(SUM[7]), .CARRY(full_adder_8_carry), .C(full_adder_7_carry), .A(A[7]), .B(B[7]));
  FULL_ADDER full_adder_9 (.SUM(SUM[8]), .CARRY(full_adder_9_carry), .C(full_adder_8_carry), .A(A[8]), .B(B[8]));
  FULL_ADDER full_adder_10 (.SUM(SUM[9]), .CARRY(full_adder_10_carry), .C(full_adder_9_carry), .A(A[9]), .B(B[9]));
  FULL_ADDER full_adder_11 (.SUM(SUM[10]), .CARRY(full_adder_11_carry), .C(full_adder_10_carry), .A(A[10]), .B(B[10]));
  FULL_ADDER full_adder_12 (.SUM(SUM[11]), .CARRY(full_adder_12_carry), .C(full_adder_11_carry), .A(A[11]), .B(B[11]));
  FULL_ADDER full_adder_13 (.SUM(SUM[12]), .CARRY(full_adder_13_carry), .C(full_adder_12_carry), .A(A[12]), .B(B[12]));
  FULL_ADDER full_adder_14 (.SUM(SUM[13]), .CARRY(full_adder_14_carry), .C(full_adder_13_carry), .A(A[13]), .B(B[13]));
  FULL_ADDER full_adder_15 (.SUM(SUM[14]), .CARRY(full_adder_15_carry), .C(full_adder_14_carry), .A(A[14]), .B(B[14]));
  FULL_ADDER full_adder_16 (.SUM(SUM[15]), .CARRY(COUT), .C(full_adder_15_carry), .A(A[15]), .B(B[15]));
endmodule
