// Digital circuit FULL ADDER.dig as structural Verilog
module FULL_ADDER (
  input  B,
  input  C,
  input  A,
  output SUM,
  output CARRY
);

  wire half_adder_1_carry, half_adder_1_sum, half_adder_2_carry;

  Half_Adder half_adder_1 (.A(C), .B(A), .SUM(half_adder_1_sum), .CARRY(half_adder_1_carry));
  Half_Adder half_adder_2 (.A(half_adder_1_sum), .B(B), .SUM(SUM), .CARRY(half_adder_2_carry));
  or or_1 (CARRY, half_adder_1_carry, half_adder_2_carry);
endmodule
