// Digital circuit PC.dig as structural Verilog
module PC (
  input  CLK,
  input  [15:0] IN,
  input  INC,
  input  LOAD,
  input  RESET,
  output [15:0] OUT
);

  wire [15:0] incrementer_1_out, multiplexer_1_out, multiplexer_2_out, multiplexer_3_out;

  incrementer incrementer_1 (.IN(OUT), .OUT(incrementer_1_out));
  Multiplexer #(.Bits(16)) multiplexer_1 (.sel(INC), .in_0(OUT), .in_1(incrementer_1_out), .out(multiplexer_1_out));
  Multiplexer #(.Bits(16)) multiplexer_2 (.sel(LOAD), .in_0(multiplexer_1_out), .in_1(IN), .out(multiplexer_2_out));
  Multiplexer #(.Bits(16)) multiplexer_3 (
    .sel(RESET), .in_0(multiplexer_2_out), .in_1({16{1'b0}}), .out(multiplexer_3_out));
  Register register_1 (.IN(multiplexer_3_out), .LOAD(1'b1), .CLK(CLK), .OUT(OUT));
endmodule
