// Digital circuit RAM4K.dig as structural Verilog
module RAM4K (
  input  [15:0] IN,
  input  CLK,
  input  LOAD,
  input  [11:0] SEL,
  output [15:0] OUT
);

  wire demultiplexer_1_out_0, demultiplexer_1_out_1, demultiplexer_1_out_2, demultiplexer_1_out_3,
       demultiplexer_1_out_4, demultiplexer_1_out_5, demultiplexer_1_out_6, demultiplexer_1_out_7;
  wire [15:0] ram512_1_out, ram512_2_out, ram512_3_out, ram512_4_out, ram512_5_out, ram512_6_out,
       ram512_7_out, ram512_8_out;

  Demultiplexer #(.Selector_Bits(3)) demultiplexer_1 (
    .sel(SEL[11:9]), .in(LOAD), .out_0(demultiplexer_1_out_0), .out_1(demultiplexer_1_out_1),
    .out_2(demultiplexer_1_out_2), .out_3(demultiplexer_1_out_3), .out_4(demultiplexer_1_out_4),
    .out_5(demultiplexer_1_out_5), .out_6(demultiplexer_1_out_6), .out_7(demultiplexer_1_out_7));
  RAM512 ram512_1 (.IN(IN), .LOAD(demultiplexer_1_out_0), .SEL(SEL[8:0]), .CLK(CLK), .OUT(ram512_1_out));
  RAM512 ram512_2 (.IN(IN), .LOAD(demultiplexer_1_out_1), .SEL(SEL[8:0]), .CLK(CLK), .OUT(ram512_2_out));
  RAM512 ram512_3 (.IN(IN), .LOAD(demultiplexer_1_out_2), .SEL(SEL[8:0]), .CLK(CLK), .OUT(ram512_3_out));
  RAM512 ram512_4 (.IN(IN), .LOAD(demultiplexer_1_out_3), .SEL(SEL[8:0]), .CLK(CLK), .OUT(ram512_4_out));
  RAM512 ram512_5 (.IN(IN), .LOAD(demultiplexer_1_out_4), .SEL(SEL[8:0]), .CLK(CLK), .OUT(ram512_5_out));
  RAM512 ram512_6 (.IN(IN), .LOAD(demultiplexer_1_out_5), .SEL(SEL[8:0]), .CLK(CLK), .OUT(ram512_6_out));
  RAM512 ram512_7 (.IN(IN), .LOAD(demultiplexer_1_out_6), .SEL(SEL[8:0]), .CLK(CLK), .OUT(ram512_7_out));
  RAM512 ram512_8 (.IN(IN), .LOAD(demultiplexer_1_out_7), .SEL(SEL[8:0]), .CLK(CLK), .OUT(ram512_8_out));
  Multiplexer #(.Selector_Bits(3), .Bits(16)) multiplexer_1 (
    .sel(SEL[11:9]), .in_0(ram512_1_out), .in_1(ram512_2_out), .in_2(ram512_3_out), .in_3(ram512_4_out),
    .in_4(ram512_5_out), .in_5(ram512_6_out), .in_6(ram512_7_out), .in_7(ram512_8_out), .out(OUT));

  // Notes on the sheet:
  //   CLK: Hz: 2
endmodule
