// Digital circuit RAM512.dig as structural Verilog
module RAM512 (
  input  [15:0] IN,
  input  CLK,
  input  LOAD,
  input  [8:0] SEL,
  output [15:0] OUT
);

  wire demultiplexer_1_out_0, demultiplexer_1_out_1, demultiplexer_1_out_2, demultiplexer_1_out_3,
       demultiplexer_1_out_4, demultiplexer_1_out_5, demultiplexer_1_out_6, demultiplexer_1_out_7;
  wire [15:0] ram64_1_out, ram64_2_out, ram64_3_out, ram64_4_out, ram64_5_out, ram64_6_out, ram64_7_out,
       ram64_8_out;

  Demultiplexer #(.Selector_Bits(3)) demultiplexer_1 (
    .sel(SEL[8:6]), .in(LOAD), .out_0(demultiplexer_1_out_0), .out_1(demultiplexer_1_out_1),
    .out_2(demultiplexer_1_out_2), .out_3(demultiplexer_1_out_3), .out_4(demultiplexer_1_out_4),
    .out_5(demultiplexer_1_out_5), .out_6(demultiplexer_1_out_6), .out_7(demultiplexer_1_out_7));
  RAM64 ram64_1 (.IN(IN), .LOAD(demultiplexer_1_out_0), .SEL(SEL[5:0]), .CLK(CLK), .OUT(ram64_1_out));
  RAM64 ram64_2 (.IN(IN), .LOAD(demultiplexer_1_out_1), .SEL(SEL[5:0]), .CLK(CLK), .OUT(ram64_2_out));
  RAM64 ram64_3 (.IN(IN), .LOAD(demultiplexer_1_out_2), .SEL(SEL[5:0]), .CLK(CLK), .OUT(ram64_3_out));
  RAM64 ram64_4 (.IN(IN), .LOAD(demultiplexer_1_out_3), .SEL(SEL[5:0]), .CLK(CLK), .OUT(ram64_4_out));
  RAM64 ram64_5 (.IN(IN), .LOAD(demultiplexer_1_out_4), .SEL(SEL[5:0]), .CLK(CLK), .OUT(ram64_5_out));
  RAM64 ram64_6 (.IN(IN), .LOAD(demultiplexer_1_out_5), .SEL(SEL[5:0]), .CLK(CLK), .OUT(ram64_6_out));
  RAM64 ram64_7 (.IN(IN), .LOAD(demultiplexer_1_out_6), .SEL(SEL[5:0]), .CLK(CLK), .OUT(ram64_7_out));
  RAM64 ram64_8 (.IN(IN), .LOAD(demultiplexer_1_out_7), .SEL(SEL[5:0]), .CLK(CLK), .OUT(ram64_8_out));
  Multiplexer #(.Selector_Bits(3), .Bits(16)) multiplexer_1 (
    .sel(SEL[8:6]), .in_0(ram64_1_out), .in_1(ram64_2_out), .in_2(ram64_3_out), .in_3(ram64_4_out),
    .in_4(ram64_5_out), .in_5(ram64_6_out), .in_6(ram64_7_out), .in_7(ram64_8_out), .out(OUT));
endmodule
