// Digital circuit RAM64.dig as structural Verilog
module RAM64 (
  input  [15:0] IN,
  input  CLK,
  input  LOAD,
  input  [5:0] SEL,
  output [15:0] OUT
);

  wire demultiplexer_1_out_0, demultiplexer_1_out_1, demultiplexer_1_out_2, demultiplexer_1_out_3,
       demultiplexer_1_out_4, demultiplexer_1_out_5, demultiplexer_1_out_6, demultiplexer_1_out_7;
  wire [15:0] ram8_1_out, ram8_2_out, ram8_3_out, ram8_4_out, ram8_5_out, ram8_6_out, ram8_7_out, ram8_8_out;

  Demultiplexer #(.Selector_Bits(3)) demultiplexer_1 (
    .sel(SEL[5:3]), .in(LOAD), .out_0(demultiplexer_1_out_0), .out_1(demultiplexer_1_out_1),
    .out_2(demultiplexer_1_out_2), .out_3(demultiplexer_1_out_3), .out_4(demultiplexer_1_out_4),
    .out_5(demultiplexer_1_out_5), .out_6(demultiplexer_1_out_6), .out_7(demultiplexer_1_out_7));
  RAM8 ram8_1 (.IN(IN), .LOAD(demultiplexer_1_out_0), .SEL(SEL[2:0]), .CLK(CLK), .OUT(ram8_1_out));
  RAM8 ram8_2 (.IN(IN), .LOAD(demultiplexer_1_out_1), .SEL(SEL[2:0]), .CLK(CLK), .OUT(ram8_2_out));
  RAM8 ram8_3 (.IN(IN), .LOAD(demultiplexer_1_out_2), .SEL(SEL[2:0]), .CLK(CLK), .OUT(ram8_3_out));
  RAM8 ram8_4 (.IN(IN), .LOAD(demultiplexer_1_out_3), .SEL(SEL[2:0]), .CLK(CLK), .OUT(ram8_4_out));
  RAM8 ram8_5 (.IN(IN), .LOAD(demultiplexer_1_out_4), .SEL(SEL[2:0]), .CLK(CLK), .OUT(ram8_5_out));
  RAM8 ram8_6 (.IN(IN), .LOAD(demultiplexer_1_out_5), .SEL(SEL[2:0]), .CLK(CLK), .OUT(ram8_6_out));
  RAM8 ram8_7 (.IN(IN), .LOAD(demultiplexer_1_out_6), .SEL(SEL[2:0]), .CLK(CLK), .OUT(ram8_7_out));
  RAM8 ram8_8 (.IN(IN), .LOAD(demultiplexer_1_out_7), .SEL(SEL[2:0]), .CLK(CLK), .OUT(ram8_8_out));
  Multiplexer #(.Bits(16), .Selector_Bits(3)) multiplexer_1 (
    .sel(SEL[5:3]), .in_0(ram8_1_out), .in_1(ram8_2_out), .in_2(ram8_3_out), .in_3(ram8_4_out),
    .in_4(ram8_5_out), .in_5(ram8_6_out), .in_6(ram8_7_out), .in_7(ram8_8_out), .out(OUT));
endmodule
