// Digital circuit Register.dig as structural Verilog
module Register (
  input  [15:0] IN,
  input  LOAD,
  input  CLK,
  output [15:0] OUT
);

  _1Bit _1bit_1 (.D(IN[0]), .EN(LOAD), .CLK(CLK), .OUT(OUT[0]));
  _1Bit _1bit_2 (.D(IN[1]), .EN(LOAD), .CLK(CLK), .OUT(OUT[1]));
  _1Bit _1bit_3 (.D(IN[2]), .EN(LOAD), .CLK(CLK), .OUT(OUT[2]));
  _1Bit _1bit_4 (.D(IN[3]), .EN(LOAD), .CLK(CLK), .OUT(OUT[3]));
  _1Bit _1bit_5 (.D(IN[4]), .EN(LOAD), .CLK(CLK), .OUT(OUT[4]));
  _1Bit _1bit_6 (.D(IN[5]), .EN(LOAD), .CLK(CLK), .OUT(OUT[5]));
  _1Bit _1bit_7 (.D(IN[6]), .EN(LOAD), .CLK(CLK), .OUT(OUT[6]));
  _1Bit _1bit_8 (.D(IN[7]), .EN(LOAD), .CLK(CLK), .OUT(OUT[7]));
  _1Bit _1bit_9 (.D(IN[8]), .EN(LOAD), .CLK(CLK), .OUT(OUT[8]));
  _1Bit _1bit_10 (.D(IN[9]), .EN(LOAD), .CLK(CLK), .OUT(OUT[9]));
  _1Bit _1bit_11 (.D(IN[10]), .EN(LOAD), .CLK(CLK), .OUT(OUT[10]));
  _1Bit _1bit_12 (.D(IN[11]), .EN(LOAD), .CLK(CLK), .OUT(OUT[11]));
  _1Bit _1bit_13 (.D(IN[12]), .EN(LOAD), .CLK(CLK), .OUT(OUT[12]));
  _1Bit _1bit_14 (.D(IN[13]), .EN(LOAD), .CLK(CLK), .OUT(OUT[13]));
  _1Bit _1bit_15 (.D(IN[14]), .EN(LOAD), .CLK(CLK), .OUT(OUT[14]));
  _1Bit _1bit_16 (.D(IN[15]), .EN(LOAD), .CLK(CLK), .OUT(OUT[15]));
endmodule
