// Digital circuit incrementer.dig as structural Verilog
module incrementer (
  input  [15:0] IN,
  output [15:0] OUT
);

  Addition addition_1 (.SUM(OUT), .A(IN), .B(16'h1), .CIN(1'b0));  // open: COUT
endmodule
